# Fritzing sketch BodenfeuchteV1.0-BreadBoard (saved by Fritzing 1.0.6)
breadboards: 1

parts:
  A1 = Firebeetle 2 ESP32-C6
  BAT1 = 18650 battery holder [package=battery-18650-kit]
  J1 = screw terminal, 2 pins
  J2 = screw terminal, 3 pins
  J3 = screw terminal, 3 pins
  J4 = screw terminal, 3 pins
  J5 = screw terminal, 3 pins
  Q1 = NTE489 JFET P-Channel [part_number=BS250P package=TO92]
  R1 = Resistor [tolerance=±5% power=0.25W resistance=1k package=THT]
  R2 = Resistor [tolerance=±5% power=0.25W resistance=10k package=THT]

nets:
  N1: A1.Pin_2, A1.Pin_31, Q1.source, R2.Pin_1
  N2: A1.Pin_4, A1.Pin_30, A1.Pin_34, BAT1.-, J1.pin2, J2.pin2, J3.pin2, J4.pin2, J5.pin2
  N3: A1.Pin_16, R1.Pin_0
  N4: A1.Pin_24, J2.pin3
  N5: A1.Pin_25, J3.pin3
  N6: A1.Pin_26, J4.pin3
  N7: A1.Pin_27, J5.pin3
  N8: A1.Pin_32, J1.pin1
  N9: A1.Pin_33, BAT1.+
  N10: J2.pin1, J3.pin1, J4.pin1, J5.pin1, Q1.drain
  N11: Q1.gate, R1.Pin_1, R2.Pin_0

custom parts:
  Firebeetle 2 ESP32-C6: FireBeetle 2 ESP32-C6 is a low-power IoT main control board designed based on the ESP32-C6 chip.
  18650 battery holder: 18650 Battery Holder
  NTE489 JFET P-Channel: An NTE489 JFET P-Channel Transistor
