# Fritzing sketch BodenfeuchteV1.0-PCB (saved by Fritzing 1.0.6)
circuit board: 8cm x 8cm
breadboards: 1

parts:
  ESP32-c6 = Firebeetle 2 ESP32-C6
  LiPo = 18650 battery holder [part_number=3.7V package=battery-18650-kit]
  Solar = screw terminal, 2 pins [part_number=5V-1W]
  Sensor1 = screw terminal, 3 pins
  Sensor2 = screw terminal, 3 pins
  Sensor3 = screw terminal, 3 pins
  Sensor4 = screw terminal, 3 pins
  MosFET = NTE489 JFET P-Channel [part_number=BS250P package=TO92]
  1kOhm = Resistor [tolerance=±5% power=0.25W resistance=1k package=THT]
  10kOhm = Resistor [tolerance=±5% power=0.25W resistance=10k package=THT]

nets:
  N1: ESP32-c6.Pin_2, ESP32-c6.Pin_31, MosFET.source, 10kOhm.Pin_1
  GND: ESP32-c6.Pin_4, ESP32-c6.Pin_30, ESP32-c6.Pin_34, LiPo.-, Solar.pin2, Sensor1.pin2, Sensor2.pin2, Sensor3.pin2, Sensor4.pin2
  N2: ESP32-c6.Pin_16, 1kOhm.Pin_0
  N3: ESP32-c6.Pin_24, Sensor1.pin3
  N4: ESP32-c6.Pin_25, Sensor2.pin3
  N5: ESP32-c6.Pin_26, Sensor3.pin3
  N6: ESP32-c6.Pin_27, Sensor4.pin3
  N7: ESP32-c6.Pin_32, Solar.pin1
  N8: ESP32-c6.Pin_33, LiPo.+
  N9: Sensor1.pin1, Sensor2.pin1, Sensor3.pin1, Sensor4.pin1, MosFET.drain
  N10: MosFET.gate, 1kOhm.Pin_1, 10kOhm.Pin_0

notes:
  FEiNT.org - Moisture Sensor (Outdoor) V1.0

custom parts:
  Firebeetle 2 ESP32-C6: FireBeetle 2 ESP32-C6 is a low-power IoT main control board designed based on the ESP32-C6 chip.
  18650 battery holder: 18650 Battery Holder
  NTE489 JFET P-Channel: An NTE489 JFET P-Channel Transistor
