# Fritzing sketch BodenfeuchteV1.4-PCB (saved by Fritzing 1.0.6)
circuit board: 8.5cm x 8.5cm
breadboards: 1

parts:
  ESP32-c6 = Firebeetle 2 ESP32-C6
  Solar = screw terminal, 2 pins [part_number=5V-1W]
  Sensor1 = screw terminal, 3 pins
  Sensor2 = screw terminal, 3 pins
  Sensor3 = screw terminal, 3 pins
  Sensor4 = screw terminal, 3 pins
  1kOhm = Resistor [tolerance=±5% power=0.25W resistance=1k package=THT]
  10kOhm = Resistor [tolerance=±5% power=0.25W resistance=10k package=THT]
  Q1 = Basic FET P-Channel [package="TO220 [THT]"]
  BAT1 = 18650 battery holder2 [package=battery-18650-kit]

nets:
  N1: ESP32-c6.Pin_2, ESP32-c6.Pin_31, 10kOhm.Pin_0, Q1.source
  GND: ESP32-c6.Pin_4, ESP32-c6.Pin_30, ESP32-c6.Pin_34, Solar.pin2, Sensor1.pin2, Sensor2.pin2, Sensor3.pin2, Sensor4.pin2, BAT1.-
  N2: ESP32-c6.Pin_16, 1kOhm.Pin_0
  N3: ESP32-c6.Pin_24, Sensor1.pin3
  N4: ESP32-c6.Pin_25, Sensor2.pin3
  N5: ESP32-c6.Pin_26, Sensor3.pin3
  N6: ESP32-c6.Pin_27, Sensor4.pin3
  N7: ESP32-c6.Pin_32, Solar.pin1
  N8: ESP32-c6.Pin_33, BAT1.+
  N9: Sensor1.pin1, Sensor2.pin1, Sensor3.pin1, Sensor4.pin1, Q1.drain
  N10: 1kOhm.Pin_1, 10kOhm.Pin_1, Q1.gate

notes:
  FEiNT.org - Moisture Sensor (Outdoor) V2.0
  BAT1

custom parts:
  Firebeetle 2 ESP32-C6: FireBeetle 2 ESP32-C6 is a low-power IoT main control board designed based on the ESP32-C6 chip.
  18650 battery holder2: 18650 Battery Holder
